# Fritzing sketch grbl4crp850 (saved by Fritzing 0.9.3b)
circuit board: 8.67055cm x 5.3342cm

parts:
  Port_2 = shrouded pin header, 26 pins [form="♂ (shrouded male)"]
  breakout = shrouded pin header, 18 pins [form="♂ (shrouded male)"]
  Part4 = Arduino Mega 2560 (Rev3)
  Port_1 = shrouded pin header, 26 pins [form="♂ (shrouded male)"]

nets:
  N1: Port_2.pin1, Part4.D8_PWM
  N2: Port_2.pin2, Part4.D10_PWM
  N3: Port_2.pin3, Part4.A3
  N4: Port_2.pin4, Part4.D11_PWM
  N5: Port_2.pin5, Part4.A4
  N6: Port_2.pin6, Part4.D12_PWM
  N7: Port_2.pin7, Part4.D42
  N8: Port_2.pin8, Port_2.pin9, Part4.A5
  N9: Port_2.pin10, breakout.pin12
  N10: Port_2.pin11, breakout.pin11
  N11: Port_2.pin12, breakout.pin10
  N12: Port_2.pin13, breakout.pin9
  N13: Port_2.pin14, Part4.5V, Port_1.pin14
  N14: Port_2.pin15, Port_2.pin16, Port_2.pin17, Port_2.pin18, Port_2.pin19, Port_2.pin20, Port_2.pin21, Port_2.pin22, breakout.pin18, Part4.GND, Port_1.pin15, Port_1.pin16, Port_1.pin17, Port_1.pin18, Port_1.pin19, Port_1.pin20, Port_1.pin21, Port_1.pin22
  N15: Port_2.pin23, breakout.pin14
  N16: Port_2.pin24, breakout.pin15
  N17: Port_2.pin25, breakout.pin16
  N18: Port_2.pin26, Part4.D44
  N19: breakout.pin1, Port_1.pin26
  N20: breakout.pin2, Port_1.pin25
  N21: breakout.pin3, Port_1.pin24
  N22: breakout.pin4, Port_1.pin23
  N23: breakout.pin5, Port_1.pin10
  N24: breakout.pin6, Port_1.pin11
  N25: breakout.pin7, Port_1.pin12
  N26: breakout.pin8, Port_1.pin13
  N27: breakout.pin17, Port_1.pin1
  N28: Part4.D24, Port_1.pin2
  N29: Part4.D25, Port_1.pin4
  N30: Part4.D26, Port_1.pin6
  N31: Part4.D27, Port_1.pin8
  N32: Part4.D29, Port_1.pin9
  N33: Part4.D30, Port_1.pin3
  N34: Part4.D31, Port_1.pin5
  N35: Part4.D32, Port_1.pin7

notes:
  https://wiki.replimat.org/wiki/grbl4crp850
  r0.3 (c) Timothy Schmidt 2021, AGPLv3+/TAPR OHL
  gnd
  5v
  spindle pwm
  2:Xstep
  1:xtra
  3:Xdir
  4:Ystep
  5:Ydir
  6:Zstep
  7:Zdir
  8:Mstep
  9:Mdir
  10:b5
  11:b6
  12:b7
  13:b8
  14:b1
  15:b2
  16:b3
  17:b4
  18
  19
  20
  21
  22
  23
  24
  25: gnd
  26: 5v
  2:X-
  3:X+
  4:Y-
  5:Y+
  6:Z+
  7:Bhome
  8:probe
  9:probe
  10:b16
  11:b17
  12:b18
  13:b9
  14
  15
  16
  17
  25
  26
  1:spindle pwm
  3.3v
  reset
  ioref
  d2
  Vin
  A0
  A1
  A2
  X+
  Y+
  probe
  A6
  A7
  A8
  A9
  A10
  A11
  A12
  A13
  2
  A15
  13
  Z+
  11:Y-
  10:X-
  9
  7
  6
  5
  4
  3
  A14
  1:tx
  0:rx
  na
  20:sda
  21:scl
  Xstep
  Ystep
  Zstep
  Mdir
  28
  Mstep
  Xdir
  Ydir
  Zdir
  33
  34
  35
  36
  37
  38
  39
  40
  41
  42
  43
  44
  45
  46
  47
  48
  49
  50
  51
  52
  53
  1
  8
  10
  11
  12
  15:nc
  Aref
  sda
  scl
